# Fritzing sketch vfd-max6921 (saved by Fritzing 0.9.3b)
circuit board: 8.46667cm x 5.64444cm
breadboards: 1

parts:
  U1 = ESP8266 NodeMCU LoLin module
  IC2 = IC, SIP package, 13 pins [chip_label=VFD]
  IC3 = IC, DIP package, 28 pins [chip_label="MAX6921 AWI"]

nets:
  N1: U1.D1, IC3.pin16
  N2: U1.D2, IC3.pin27
  N3: U1.3V3, IC2.pin1, IC3.pin28
  N4: U1.D8, IC3.pin15
  N5: IC2.pin2, IC3.pin26
  N6: IC2.pin3, IC3.pin25
  N7: IC2.pin4, IC3.pin24
  N8: IC2.pin5, IC3.pin23
  N9: IC2.pin6, IC3.pin20
  N10: IC2.pin7, IC3.pin11
  N11: IC2.pin8, IC3.pin10
  N12: IC2.pin9, IC3.pin9
  N13: IC2.pin10, IC3.pin8
  N14: IC2.pin11, IC3.pin7
  N15: IC2.pin12, IC3.pin6
  GND: IC2.pin13, IC3.pin14
  12V: IC3.pin1

custom parts:
  ESP8266 NodeMCU LoLin module: ESP8266 based NodeMCU
